# Fritzing sketch pi_relay (saved by Fritzing 0.9.3b)

parts:
  Raspberry_Pi_2 = Raspberry Pi 4 [part_number=RPI-4-b]
  U2 = 2-Channel 5v Relay Shield [package=relay-2ch5v10a]

nets:
  N1: Raspberry_Pi_2.GPIO2, U2.IN1
  N2: Raspberry_Pi_2.GPIO3, U2.IN2
  GND: Raspberry_Pi_2.GND, U2.GND
  5V: Raspberry_Pi_2.5V, U2.VCC

custom parts:
  Raspberry Pi 4: The RPi4, a faster version of the awesome Raspberry Pi 2 B ARM Board with 40 pin gpio. Ready for special Raspberry Pi B+ and RPi2 Hat (Hardware attached (on) top)
  2-Channel 5v Relay Shield: 2 Channel 5v Relay Shield w. 2x SPD-06VDC-SD-C
