# Fritzing sketch pi_rgb (saved by Fritzing 0.9.3b)
breadboards: 1

parts:
  Raspberry_Pi_2 = Raspberry Pi 4 [part_number=RPI-4-b]
  LED1 = RGB LED (com. anode, rbg) [package="5 mm [THT]"]

nets:
  N1: Raspberry_Pi_2.GND, LED1.green_cathode
  N2: Raspberry_Pi_2.GPIO7, LED1.blue_cathode
  N3: Raspberry_Pi_2.GPIO8, LED1.common_anode
  N4: Raspberry_Pi_2.GPIO25, LED1.red_cathode

custom parts:
  Raspberry Pi 4: The RPi4, a faster version of the awesome Raspberry Pi 2 B ARM Board with 40 pin gpio. Ready for special Raspberry Pi B+ and RPi2 Hat (Hardware attached (on) top)
